// Digital circuit atk16_decoder.dig as structural Verilog
module atk16_decoder (
  input  [15:0] DBUS,
  input  IR_IE,
  input  CLK,
  input  JA_OE,
  output [2:0] RW_S,
  output [2:0] R1_S,
  output [2:0] R2_S,
  output [3:0] ALU_S,
  output [3:0] OP
);

  Register #(.Bits(16)) IR (.D(DBUS), .C(CLK), .en(IR_IE), .Q({OP[3:1], ALU_S[3], R1_S, R2_S, ALU_S[2:0], RW_S}));
  assign DBUS = JA_OE ? {{7{1'b0}}, R1_S, R2_S, ALU_S[2:0]} : 16'bz;  // Driver driver_1
  // Pins of 1 and 3 bits meet at RW_S
  // Pins of 1 and 3 bits meet at R1_S
  // Pins of 1 and 3 bits meet at R2_S

  assign OP[0] = ALU_S[3];

  // Notes on the sheet:
  //   RW_S: Write register selection
  //   R1_S: Read register 1 selection
  //   R2_S: Read register 2 selection
  //   IR_IE: Instruction register input enable
  //   ALU_S: ALU selection code
  //   JA_OE: Jump address output enable
  //   OP: Opcode
endmodule
