// Digital circuit atk16_ppu.dig as structural Verilog
module atk16_ppu (
  input  PCLK,
  input  CLK,
  input  MMIO_IE,
  input  MMIO_OE,
  input  [15:0] DBUS,
  input  [12:0] MMIO_S
);

  wire and_1_out, comparator_1_gt, comparator_2_gt, comparator_3_gt, comparator_4_lt, comparator_5_gt,
       comparator_6_lt, HSYNC, VSYNC;
  wire [1:0] PB, PG, PR;
  wire [3:0] SCAN_BUFFER_d;
  wire [8:0] X, Y;
  wire [9:0] counter_1_out, counter_2_out;
  wire [9:9] sub_1_s, sub_2_s;
  wire [10:0] SMEMBUS;

  and and_1 (and_1_out, MMIO_S[11], ~MMIO_S[12]);  // And
  RAMDualPort #(.AddrBits(11), .Bits(16)) SPRITE_MEM (
    .A(SMEMBUS), .Din(DBUS), .str(MMIO_IE), .C(CLK), .ld(MMIO_OE));  // open: D
  Multiplexer #(.Bits(11)) multiplexer_1 (.sel(and_1_out), .in_0({11{1'b0}}), .in_1(MMIO_S[10:0]), .out(SMEMBUS));
  VGA vga_1 (.R(PR), .G(PG), .B(PB), .H(HSYNC), .V(VSYNC), .C(PCLK));
  RAMDualPort #(.AddrBits(9), .Bits(4)) SCAN_BUFFER (
    .A(X), .Din(4'b0000), .str(1'b0), .C(1'b0), .ld(1'b0), .D(SCAN_BUFFER_d));
  Counter #(.Bits(10)) counter_1 (.en(1'b1), .C(PCLK), .clr(comparator_1_gt), .out(counter_1_out));  // open: ovf
  Counter #(.Bits(10)) counter_2 (
    .en(1'b1), .C(comparator_1_gt), .clr(comparator_2_gt), .out(counter_2_out));  // open: ovf
  // atk16_ppu_palette atk16_ppu_palette_1: pin names not known; wires that end beside it: SCAN_BUFFER_d[3], SCAN_BUFFER_d[2], SCAN_BUFFER_d[1], SCAN_BUFFER_d[0]
  Comparator #(.Bits(10)) comparator_1 (.a(counter_1_out), .b(10'h31e), .gt(comparator_1_gt));  // open: eq, lt
  Comparator #(.Bits(10)) comparator_2 (.a(counter_2_out), .b(10'h20b), .gt(comparator_2_gt));  // open: eq, lt
  Comparator #(.Bits(10)) comparator_3 (.a(counter_1_out), .b(10'h10), .gt(comparator_3_gt));  // open: eq, lt
  Comparator #(.Bits(10)) comparator_4 (.a(counter_1_out), .b(10'h71), .lt(comparator_4_lt));  // open: gt, eq
  Sub #(.Bits(10)) sub_1 (.a(counter_1_out), .b(10'ha0), .c_i(1'b0), .s({sub_1_s[9], X}));  // open: c_o
  Comparator #(.Bits(10)) comparator_5 (.a(counter_2_out), .b(10'ha), .gt(comparator_5_gt));  // open: eq, lt
  Comparator #(.Bits(10)) comparator_6 (.a(counter_2_out), .b(10'hd), .lt(comparator_6_lt));  // open: gt, eq
  Sub #(.Bits(10)) sub_2 (.a(counter_2_out), .b(10'h2d), .c_i(1'b0), .s({sub_2_s[9], Y}));  // open: c_o
  nand nand_1 (HSYNC, comparator_3_gt, comparator_4_lt);
  nand nand_2 (VSYNC, comparator_5_gt, comparator_6_lt);

  // Notes on the sheet:
  //   PCLK: Pixel clock
  //   CLK: CPU clock
  //   DBUS: Data bus
  //   MMIO_S: MMI/O selector
  //   (8 pixels wide x 8 pixels tall + 12 bit X + 12 bit Y + 8 bit priority)
  //   x 21 sprites
  //   < 2**11 = 2048 words
  //   2**11 selector addresses for
  //   sprite mem, starting from 0x0800
  //   Div 2
endmodule
