// Digital circuit atk16_regbank.dig as structural Verilog
module atk16_regbank (
  input  [15:0] Din,
  input  RW_IE,
  input  [2:0] RW_S,
  input  CLK,
  input  [2:0] R1_S,
  input  [2:0] R2_S,
  output [15:0] D1,
  output [15:0] D2
);

  wire and_1_out, and_2_out, and_3_out, and_4_out, and_5_out, and_6_out, and_7_out, RW_A, RW_B, RW_C, RW_D,
       RW_E, RW_F, RW_G;
  wire [15:0] Q1, Q2, Q3, Q4, Q5, Q6, Q7;

  Decoder #(.Selector_Bits(3)) decoder_1 (
    .sel(RW_S), .out_1(RW_A), .out_2(RW_B), .out_3(RW_C), .out_4(RW_D), .out_5(RW_E), .out_6(RW_F),
    .out_7(RW_G));  // open: out_0
  and and_1 (and_1_out, RW_IE, RW_A);
  and and_2 (and_2_out, RW_IE, RW_B);
  and and_3 (and_3_out, RW_IE, RW_C);
  and and_4 (and_4_out, RW_IE, RW_D);
  and and_5 (and_5_out, RW_IE, RW_E);
  and and_6 (and_6_out, RW_IE, RW_F);
  and and_7 (and_7_out, RW_IE, RW_G);
  Register #(.Bits(16)) RA (.D(Din), .C(CLK), .en(and_1_out), .Q(Q1));
  Register #(.Bits(16)) RB (.D(Din), .C(CLK), .en(and_2_out), .Q(Q2));
  Register #(.Bits(16)) RC (.D(Din), .C(CLK), .en(and_3_out), .Q(Q3));
  Register #(.Bits(16)) RD (.D(Din), .C(CLK), .en(and_4_out), .Q(Q4));
  Register #(.Bits(16)) RE (.D(Din), .C(CLK), .en(and_5_out), .Q(Q5));
  Register #(.Bits(16)) RF (.D(Din), .C(CLK), .en(and_6_out), .Q(Q6));
  Register #(.Bits(16)) RG (.D(Din), .C(CLK), .en(and_7_out), .Q(Q7));
  Multiplexer #(.Selector_Bits(3), .Bits(16)) multiplexer_1 (
    .sel(R1_S), .in_0({16{1'b0}}), .in_1(Q1), .in_2(Q2), .in_3(Q3), .in_4(Q4), .in_5(Q5), .in_6(Q6),
    .in_7(Q7), .out(D1));
  Multiplexer #(.Selector_Bits(3), .Bits(16)) multiplexer_2 (
    .sel(R2_S), .in_0({16{1'b0}}), .in_1(Q1), .in_2(Q2), .in_3(Q3), .in_4(Q4), .in_5(Q5), .in_6(Q6),
    .in_7(Q7), .out(D2));

  // Notes on the sheet:
  //   Din: Data bus in
  //   D1: Read register 1 data out
  //   D2: Read register 2 data out
  //   RW_IE: Write register input enable
  //   RW_S: Write register select
  //   CLK: Clock
  //   R1_S: Read register 1 select
  //   R2_S: Read register 2 select
endmodule

/* Test case:
CLK Din RW_IE RW_S R1_S R2_S D1  D2
# store and read from RA works
C   0xF 1     1    0    X    X   X
C   0   0     0    1    X    0xF X
C   0x5 1     1    1    X    0x5 X
C   0   0     0    1    X    0x5 X

# zero register read and write
C   0xA 1     0    0    X    0   X
*/
