// Digital circuit atk16_tpu.dig as structural Verilog
module atk16_tpu (
  input  MMIO_IE,
  input  MMIO_OE,
  input  [12:0] MMIO_S,
  input  [15:0] DBUS,
  input  [8:0] X,
  input  [7:0] Y,
  input  PCLK,
  output [1:0] PR,
  output [1:0] PG,
  output [1:0] PB
);

  wire CLK, MMIOMATCH;
  wire [7:0] CHAR_S, CHARMEM_d;
  wire [10:0] multiplexer_1_out;

  and and_1 (MMIOMATCH, MMIO_S[11], MMIO_S[12], MMIO_IE);
  Counter CLK_divider__4 (.en(1'b1), .C(PCLK), .clr(1'b0), .ovf(CLK));  // open: out
  Multiplexer #(.Bits(11)) multiplexer_1 (
    .sel(MMIOMATCH), .in_0({Y[7:3], X[8:3]}), .in_1(MMIO_S[10:0]), .out(multiplexer_1_out));
  RAMDualPort #(.AddrBits(11), .Bits(8)) TEXTMEM (
    .A(multiplexer_1_out), .Din(DBUS[7:0]), .str(MMIOMATCH), .C(CLK), .ld(1'b1), .D(CHAR_S));
  // Probe on CHAR_S
  EEPROM #(.AddrBits(11), .Bits(8)) CHARMEM (.A({CHAR_S, Y[2:0]}), .CS(1'b1), .WE(1'b0), .OE(1'b1), .D(CHARMEM_d));
  // Probe on CHARMEM_d
  BitSelector #(.Selector_Bits(3)) bitselector_1 (.in(CHARMEM_d), .sel(X[2:0]), .out(PB[1]));
  // Probe on X[2:0]
  // Probe on PB[1]

  assign PB[0] = PB[1];
  assign PG = {2{PB[1]}};
  assign PR = {2{PB[1]}};

  // Other names for the same wires on the sheet: CCOLOR = PB[1]; DBUS_L8[7:0] = DBUS[7:0];
  //   MMIOADDR[10:0] = MMIO_S[10:0]; CX[2:0] = X[2:0]; TX[5:0] = X[8:3]; CY[2:0] = Y[2:0]; TY[4:0] = Y[7:3]

  // Notes on the sheet:
  //   MMIO_S: MMI/O selector
  //   DBUS: Data bus
  //   X: X pixel
  //   Y: Y pixel
  //   PCLK: Pixel clock
  //   contents of CHARMEM (hex, n*v repeats v):
  //   8*0,c,1e,33,33,3f,33,33,0,3f,66,66,3e,66,66,3f,0,3c,66,3,3,3,66
  //   ,3c,0,1f,36,66,66,66,36,1f,0,7f,46,16,1e,16,46,7f,0,7f,46,16,1e
  //   ,16,6,f,0,3c,66,3,3,73,66,7c,0,33,33,33,3f,33,33,33,0,1e,5*c,1e
  //   ,0,78,30,30,30,33,33,1e,0,67,66,36,1e,36,66,67,0,f,6,6,6,46,66
  //   ,7f,0,63,77,7f,7f,6b,63,63,0,63,67,6f,7b,73,63,63,0,1c,36,63,63,63
  //   ,36,1c,0,3f,66,66,3e,6,6,f,0,1e,33,33,33,3b,1e,38,0,3f,66,66,3e
  //   ,36,66,67,0,1e,33,6,c,18,33,1e,0,3f,2d,4*c,1e,0,6*33,3f,0,5*33
  //   ,1e,c,0,63,63,63,6b,7f,77,63,0,63,63,36,1c,36,63,63,0,33,33,33
  //   ,1e,c,c,1e,0,7f,63,31,18,4c,66,7f
endmodule
